// Logisim project 50logic_circuit_all_50.circ as structural Verilog: 50 circuits, main circuit 01_1_to_4_demultiplexer
module _01_1_to_4_demultiplexer (
  input  D,
  input  S1,
  input  S0,
  output Y0,
  output Y1,
  output Y2,
  output Y3
);

  wire not_1_out, not_2_out;

  not not_1 (not_1_out, S1);
  not not_2 (not_2_out, S0);
  and and_1 (Y0, not_1_out, not_2_out, D);
  and and_2 (Y1, not_1_out, S0, D);
  and and_3 (Y2, S1, not_2_out, D);
  and and_4 (Y3, S1, S0, D);

  // Notes on the sheet:
  //   1-to-4 demultiplexer
  //   One data input; S1 is the most-significant select bit.
endmodule

module _02_2_to_4_decoder (
  input  A,
  input  B,
  output Y0,
  output Y1,
  output Y2,
  output Y3
);

  wire not_1_out, not_2_out;

  not not_1 (not_1_out, A);
  not not_2 (not_2_out, B);
  and and_1 (Y0, not_1_out, not_2_out);
  and and_2 (Y1, not_1_out, B);
  and and_3 (Y2, A, not_2_out);
  and and_4 (Y3, A, B);

  // Notes on the sheet:
  //   2-to-4 decoder
  //   Active-high outputs; A is the most-significant input bit.
endmodule

module _03_3_to_8_decoder (
  input  A,
  input  B,
  input  C,
  output Y0,
  output Y1,
  output Y2,
  output Y3,
  output Y4,
  output Y5,
  output Y6,
  output Y7
);

  wire not_1_out, not_2_out, not_3_out;

  not not_1 (not_1_out, A);
  not not_2 (not_2_out, B);
  not not_3 (not_3_out, C);
  and and_1 (Y0, not_1_out, not_2_out, not_3_out);
  and and_2 (Y1, not_1_out, not_2_out, C);
  and and_3 (Y2, not_1_out, B, not_3_out);
  and and_4 (Y3, not_1_out, B, C);
  and and_5 (Y4, A, not_2_out, not_3_out);
  and and_6 (Y5, A, not_2_out, C);
  and and_7 (Y6, A, B, not_3_out);
  and and_8 (Y7, A, B, C);

  // Notes on the sheet:
  //   3-to-8 decoder
  //   Active-high outputs; A is the most-significant input bit.
endmodule

module _04_4_to_1_multiplexer (
  input  S1,
  input  S0,
  input  D0,
  input  D1,
  input  D2,
  input  D3,
  output Y
);

  wire and_1_out, and_2_out, and_3_out, and_4_out, not_1_out, not_2_out, or_1_out, or_2_out;

  not not_1 (not_1_out, S1);
  not not_2 (not_2_out, S0);
  and and_1 (and_1_out, not_1_out, not_2_out, D0);
  and and_2 (and_2_out, not_1_out, S0, D1);
  and and_3 (and_3_out, S1, not_2_out, D2);
  and and_4 (and_4_out, S1, S0, D3);
  or or_1 (or_1_out, and_1_out, and_2_out);
  or or_2 (or_2_out, and_3_out, and_4_out);
  or or_3 (Y, or_1_out, or_2_out);

  // Notes on the sheet:
  //   4-to-1 multiplexer
  //   S1 is the most-significant select bit; D0 is selected by S1S0=00.
endmodule

module _05_8_to_1_multiplexer (
  input  S2,
  input  S1,
  input  S0,
  input  D0,
  input  D1,
  input  D2,
  input  D3,
  input  D4,
  input  D5,
  input  D6,
  input  D7,
  output Y
);

  wire and_1_out, and_2_out, and_3_out, and_4_out, and_5_out, and_6_out, and_7_out, and_8_out, and_9_out,
       and_10_out, and_11_out, and_12_out, and_13_out, and_14_out, and_15_out, and_16_out, not_1_out,
       not_2_out, not_3_out, or_1_out, or_2_out, or_3_out;

  not not_1 (not_1_out, S2);
  not not_2 (not_2_out, S1);
  not not_3 (not_3_out, S0);
  and and_1 (and_1_out, not_1_out, not_2_out, not_3_out);
  and and_2 (and_2_out, not_1_out, not_2_out, S0);
  and and_3 (and_3_out, not_1_out, S1, not_3_out);
  and and_4 (and_4_out, not_1_out, S1, S0);
  and and_5 (and_5_out, S2, not_2_out, not_3_out);
  and and_6 (and_6_out, S2, not_2_out, S0);
  and and_7 (and_7_out, S2, S1, not_3_out);
  and and_8 (and_8_out, S2, S1, S0);
  and and_9 (and_9_out, and_1_out, D0);
  and and_10 (and_10_out, and_2_out, D1);
  and and_11 (and_11_out, and_3_out, D2);
  and and_12 (and_12_out, and_4_out, D3);
  and and_13 (and_13_out, and_5_out, D4);
  and and_14 (and_14_out, and_6_out, D5);
  and and_15 (and_15_out, and_7_out, D6);
  and and_16 (and_16_out, and_8_out, D7);
  or or_1 (or_1_out, and_9_out, and_10_out, and_11_out);
  or or_2 (or_2_out, and_12_out, and_13_out, and_14_out);
  or or_3 (or_3_out, and_15_out, and_16_out);
  or or_4 (Y, or_1_out, or_2_out, or_3_out);

  // Notes on the sheet:
  //   8-to-1 multiplexer
  //   S2 is the most-significant select bit; D0 is selected by S2S1S0=000.
endmodule

module _06_Octal_to_binary_encoder (
  input  D0,
  input  D1,
  input  D2,
  input  D3,
  input  D4,
  input  D5,
  input  D6,
  input  D7,
  output B2,
  output B1,
  output B0
);

  wire or_1_out, or_2_out, or_3_out, or_4_out, or_5_out;

  or or_1 (or_1_out, D4, D5);
  or or_2 (or_2_out, D6, D7);
  or or_3 (or_3_out, D2, D3);
  or or_4 (or_4_out, D1, D3);
  or or_5 (or_5_out, D5, D7);
  or or_6 (B2, or_1_out, or_2_out);
  or or_7 (B1, or_3_out, or_2_out);
  or or_8 (B0, or_4_out, or_5_out);

  // Notes on the sheet:
  //   Octal-to-binary encoder
  //   One-hot inputs D0-D7; outputs are B2 B1 B0.
endmodule

module _07_Decimal_to_BCD_encoder (
  input  D0,
  input  D1,
  input  D2,
  input  D3,
  input  D4,
  input  D5,
  input  D6,
  input  D7,
  input  D8,
  input  D9,
  output B3,
  output B2,
  output B1,
  output B0
);

  wire or_1_out, or_2_out, or_3_out, or_4_out, or_5_out;

  or or_1 (or_1_out, D4, D5);
  or or_2 (or_2_out, D6, D7);
  or or_3 (or_3_out, D2, D3);
  or or_4 (or_4_out, D1, D3, D5);
  or or_5 (or_5_out, D7, D9);
  or or_6 (B3, D8, D9);
  or or_7 (B2, or_1_out, or_2_out);
  or or_8 (B1, or_3_out, or_2_out);
  or or_9 (B0, or_4_out, or_5_out);

  // Notes on the sheet:
  //   Decimal-to-BCD encoder
  //   One-hot decimal inputs D0-D9; B3 B2 B1 B0 is the BCD result.
endmodule

module _08_2_to_1_multiplexer (
  input  S,
  input  D0,
  input  D1,
  output Y
);

  wire and_1_out, and_2_out, not_1_out;

  not not_1 (not_1_out, S);
  and and_1 (and_1_out, not_1_out, D0);
  and and_2 (and_2_out, S, D1);
  or or_1 (Y, and_1_out, and_2_out);

  // Notes on the sheet:
  //   2-to-1 multiplexer
  //   S=0 selects D0; S=1 selects D1.
endmodule

module _09_3_bit_even_parity_generator_using_NAND_gates (
  input  A,
  input  B,
  input  C,
  output P
);

  wire nand_1_out, nand_2_out, nand_3_out, nand_4_out, nand_5_out, nand_6_out, nand_7_out;

  nand nand_1 (nand_1_out, A, B);
  nand nand_2 (nand_2_out, A, nand_1_out);
  nand nand_3 (nand_3_out, B, nand_1_out);
  nand nand_4 (nand_4_out, nand_2_out, nand_3_out);
  nand nand_5 (nand_5_out, nand_4_out, C);
  nand nand_6 (nand_6_out, nand_4_out, nand_5_out);
  nand nand_7 (nand_7_out, C, nand_5_out);
  nand nand_8 (P, nand_6_out, nand_7_out);

  // Notes on the sheet:
  //   3-bit even parity generator using NAND gates
  //   P=A XOR B XOR C; P makes the total number of 1s even.
endmodule

module _10_4_bit_even_parity_generator_using_NAND_gates (
  input  A,
  input  B,
  input  C,
  input  D,
  output P
);

  wire nand_1_out, nand_2_out, nand_3_out, nand_4_out, nand_5_out, nand_6_out, nand_7_out, nand_8_out,
       nand_9_out, nand_10_out, nand_11_out;

  nand nand_1 (nand_1_out, A, B);
  nand nand_2 (nand_2_out, C, D);
  nand nand_3 (nand_3_out, A, nand_1_out);
  nand nand_4 (nand_4_out, B, nand_1_out);
  nand nand_5 (nand_5_out, C, nand_2_out);
  nand nand_6 (nand_6_out, D, nand_2_out);
  nand nand_7 (nand_7_out, nand_3_out, nand_4_out);
  nand nand_8 (nand_8_out, nand_5_out, nand_6_out);
  nand nand_9 (nand_9_out, nand_7_out, nand_8_out);
  nand nand_10 (nand_10_out, nand_7_out, nand_9_out);
  nand nand_11 (nand_11_out, nand_8_out, nand_9_out);
  nand nand_12 (P, nand_10_out, nand_11_out);

  // Notes on the sheet:
  //   4-bit even parity generator using NAND gates
  //   P=A XOR B XOR C XOR D; P makes the total number of 1s even.
endmodule

module _11_AND_gate_using_NAND_gate (
  input  A,
  input  B,
  output Y
);

  wire nand_1_out;

  nand nand_1 (nand_1_out, A, B);
  nand nand_2 (Y, nand_1_out, nand_1_out);

  // Notes on the sheet:
  //   AND gate using NAND gate
  //   NAND followed by NAND inversion.
endmodule

module _12_AND_gate_using_NOR_gate (
  input  A,
  input  B,
  output Y
);

  wire nor_1_out, nor_2_out;

  nor nor_1 (nor_1_out, A, A);
  nor nor_2 (nor_2_out, B, B);
  nor nor_3 (Y, nor_1_out, nor_2_out);

  // Notes on the sheet:
  //   AND gate using NOR gate
  //   Invert each input with NOR, then NOR the inverted inputs.
endmodule

module _13_D_flip_flop_using_NAND_gates (
  input  D,
  input  CLK,
  output Q,
  output Qbar
);

  wire nand_1_out, nand_2_out, nand_3_out;

  nand nand_1 (nand_1_out, D, D);
  nand nand_2 (nand_2_out, D, CLK);
  nand nand_3 (nand_3_out, CLK, nand_1_out);
  nand nand_4 (Q, nand_2_out, Qbar);
  nand nand_5 (Qbar, Q, nand_3_out);

  // Notes on the sheet:
  //   D flip-flop using NAND gates
  //   Gated D Flip-Flop constructed with 5 NAND gates.
endmodule

module _14_Excess_3_code_conversion_from_BCD (
  input  A,
  input  B,
  input  C,
  input  D,
  output E3,
  output E2,
  output E1,
  output E0
);

  wire and_1_out, and_2_out, and_3_out, and_4_out, and_5_out, and_6_out, and_7_out, not_1_out, not_2_out;

  not not_1 (not_1_out, B);
  not not_2 (not_2_out, C);
  not not_3 (E0, D);
  and and_1 (and_1_out, B, D);
  and and_2 (and_2_out, B, C);
  and and_3 (and_3_out, not_1_out, C);
  and and_4 (and_4_out, not_1_out, D);
  and and_5 (and_5_out, B, not_2_out, E0);
  and and_6 (and_6_out, C, D);
  and and_7 (and_7_out, not_2_out, E0);
  or or_1 (E3, A, and_1_out, and_2_out);
  or or_2 (E2, and_3_out, and_4_out, and_5_out);
  or or_3 (E1, and_6_out, and_7_out);

  // Notes on the sheet:
  //   Excess-3 code conversion from BCD
  //   For valid BCD A B C D, outputs equal the binary value plus 0011.
endmodule

module _15_Full_adder (
  input  A,
  input  B,
  input  Cin,
  output S,
  output Cout
);

  wire and_1_out, and_2_out, xor_1_out;

  xor xor_1 (xor_1_out, A, B);
  and and_1 (and_1_out, A, B);
  xor xor_2 (S, xor_1_out, Cin);
  and and_2 (and_2_out, xor_1_out, Cin);
  or or_1 (Cout, and_1_out, and_2_out);

  // Notes on the sheet:
  //   Full adder
  //   S=A XOR B XOR Cin; Cout=AB + Cin(A XOR B).
endmodule

module _16_Full_subtractor (
  input  A,
  input  B,
  input  Bin,
  output Diff,
  output Bout
);

  wire and_1_out, and_2_out, not_1_out, not_2_out, xor_1_out;

  xor xor_1 (xor_1_out, A, B);
  not not_1 (not_1_out, A);
  xor xor_2 (Diff, xor_1_out, Bin);
  not not_2 (not_2_out, xor_1_out);
  and and_1 (and_1_out, not_1_out, B);
  and and_2 (and_2_out, not_2_out, Bin);
  or or_1 (Bout, and_1_out, and_2_out);

  // Notes on the sheet:
  //   Full subtractor
  //   Diff=A XOR B XOR Bin; Bout=A'B + (A XNOR B)Bin.
endmodule

module _17_Half_adder (
  input  A,
  input  B,
  output S,
  output Carry
);

  xor xor_1 (S, A, B);
  and and_1 (Carry, A, B);

  // Notes on the sheet:
  //   Half adder
  //   S=A XOR B; Carry=AB.
endmodule

module _18_Half_subtractor (
  input  A,
  input  B,
  output Diff,
  output Borrow
);

  wire not_1_out;

  not not_1 (not_1_out, A);
  xor xor_1 (Diff, A, B);
  and and_1 (Borrow, not_1_out, B);

  // Notes on the sheet:
  //   Half subtractor
  //   Diff=A XOR B; Borrow=A'B.
endmodule

module _19_F_A_B_C_A_B_BC_AC (
  input  A,
  input  B,
  input  C,
  output F
);

  wire and_1_out, and_2_out, and_3_out, not_1_out, not_2_out;

  not not_1 (not_1_out, A);
  not not_2 (not_2_out, C);
  and and_1 (and_1_out, not_1_out, B);
  and and_2 (and_2_out, B, not_2_out);
  and and_3 (and_3_out, A, C);
  or or_1 (F, and_1_out, and_2_out, and_3_out);

  // Notes on the sheet:
  //   F(A,B,C) = A'B + BC' + AC
  //   Representative expression used because the index page does not specify F.
endmodule

module _20_F_A_B_C_A_B_BC_AC (
  input  A,
  input  B,
  input  C,
  output F
);

  wire nand_1_out, nand_2_out, nand_3_out, nand_4_out, nand_5_out;

  nand nand_1 (nand_1_out, A, A);
  nand nand_2 (nand_2_out, C, C);
  nand nand_3 (nand_3_out, nand_1_out, B);
  nand nand_4 (nand_4_out, B, nand_2_out);
  nand nand_5 (nand_5_out, A, C);
  nand nand_6 (F, nand_3_out, nand_4_out, nand_5_out);

  // Notes on the sheet:
  //   F(A,B,C) = A'B + BC' + AC
  //   NAND-only realization of F(A,B,C) = A'B + BC' + AC.
endmodule

module _21_JK_flip_flop_using_NAND_gates (
  input  J,
  input  CLK,
  input  K,
  input  CLR_bar,
  output Q,
  output Q_bar
);

  wire nand_1_out, nand_2_out, nand_3_out, nand_4_out, nand_5_out, nand_6_out, nand_7_out;

  nand nand_1 (nand_1_out, Q_bar, J, CLK);
  nand nand_2 (nand_2_out, CLK, K, Q);
  nand nand_3 (nand_3_out, nand_1_out, nand_4_out);
  nand nand_4 (nand_4_out, nand_3_out, CLR_bar, nand_2_out);
  nand nand_5 (nand_5_out, CLK, CLK);
  nand nand_6 (nand_6_out, nand_3_out, nand_5_out);
  nand nand_7 (nand_7_out, nand_5_out, nand_4_out);
  nand nand_8 (Q, nand_6_out, Q_bar);
  nand nand_9 (Q_bar, nand_7_out, CLR_bar, Q);

  // Notes on the sheet:
  //   JK flip-flop using NAND gates
  //   Race-free Master-Slave JK Flip-Flop using NAND gates with active-low CLR_bar.
endmodule

module _22_Hexadecimal_to_binary_encoder (
  input  D0,
  input  D1,
  input  D2,
  input  D3,
  input  D4,
  input  D5,
  input  D6,
  input  D7,
  input  D8,
  input  D9,
  input  DA,
  input  DB,
  input  DC,
  input  DD,
  input  DE,
  input  DF,
  output B3,
  output B2,
  output B1,
  output B0
);

  wire or_1_out, or_2_out, or_3_out, or_4_out, or_5_out, or_6_out, or_7_out, or_8_out, or_9_out, or_10_out,
       or_11_out, or_12_out;

  or or_1 (or_1_out, D8, D9, DA);
  or or_2 (or_2_out, DB, DC, DD);
  or or_3 (or_3_out, DE, DF);
  or or_4 (or_4_out, D4, D5, D6);
  or or_5 (or_5_out, D7, DC, DD);
  or or_6 (or_6_out, DE, DF);
  or or_7 (or_7_out, D2, D3, D6);
  or or_8 (or_8_out, D7, DA, DB);
  or or_9 (or_9_out, DE, DF);
  or or_10 (or_10_out, D1, D3, D5);
  or or_11 (or_11_out, D7, D9, DB);
  or or_12 (or_12_out, DD, DF);
  or or_13 (B3, or_1_out, or_2_out, or_3_out);
  or or_14 (B2, or_4_out, or_5_out, or_6_out);
  or or_15 (B1, or_7_out, or_8_out, or_9_out);
  or or_16 (B0, or_10_out, or_11_out, or_12_out);

  // Notes on the sheet:
  //   Hexadecimal-to-binary encoder
  //   One-hot inputs D0-DF; outputs are B3 B2 B1 B0.
endmodule

module _23_NAND_gate_using_NOR_gates (
  input  A,
  input  B,
  output Y
);

  wire nor_1_out, nor_2_out, nor_3_out;

  nor nor_1 (nor_1_out, A, A);
  nor nor_2 (nor_2_out, B, B);
  nor nor_3 (nor_3_out, nor_1_out, nor_2_out);
  nor nor_4 (Y, nor_3_out, nor_3_out);

  // Notes on the sheet:
  //   NAND gate using NOR gates
  //   NOR-only realization of Y=(AB)'.
endmodule

module _24_NOR_gate_using_NAND_gates (
  input  A,
  input  B,
  output Y
);

  wire nand_1_out, nand_2_out, nand_3_out;

  nand nand_1 (nand_1_out, A, A);
  nand nand_2 (nand_2_out, B, B);
  nand nand_3 (nand_3_out, nand_1_out, nand_2_out);
  nand nand_4 (Y, nand_3_out, nand_3_out);

  // Notes on the sheet:
  //   NOR gate using NAND gates
  //   NAND-only realization of Y=(A+B)'.
endmodule

module _25_OR_gate_using_NAND_gates (
  input  A,
  input  B,
  output Y
);

  wire nand_1_out, nand_2_out;

  nand nand_1 (nand_1_out, A, A);
  nand nand_2 (nand_2_out, B, B);
  nand nand_3 (Y, nand_1_out, nand_2_out);

  // Notes on the sheet:
  //   OR gate using NAND gates
  //   Invert inputs with NAND gates, then NAND them.
endmodule

module _26_OR_gate_using_NOR_gates (
  input  A,
  input  B,
  output Y
);

  wire nor_1_out;

  nor nor_1 (nor_1_out, A, B);
  nor nor_2 (Y, nor_1_out, nor_1_out);

  // Notes on the sheet:
  //   OR gate using NOR gates
  //   NOR followed by NOR inversion.
endmodule

module _27_Clocked_SR_latch_using_NAND_gates (
  input  S,
  input  EN,
  input  R,
  output Q,
  output Qbar
);

  wire nand_1_out, nand_2_out;

  nand nand_1 (nand_1_out, S, EN);
  nand nand_2 (nand_2_out, EN, R);
  nand nand_3 (Q, nand_1_out, Qbar);
  nand nand_4 (Qbar, Q, nand_2_out);

  // Notes on the sheet:
  //   Clocked SR latch using NAND gates
  //   Clock/enable is level-sensitive.
endmodule

module _28_Clocked_SR_latch_using_NOR_gates (
  input  R,
  input  EN,
  input  S,
  output Q,
  output Qbar
);

  wire nor_1_out, nor_2_out, nor_3_out, nor_4_out, nor_5_out;

  nor nor_1 (nor_1_out, R, R);
  nor nor_2 (nor_2_out, EN, EN);
  nor nor_3 (nor_3_out, S, S);
  nor nor_4 (nor_4_out, nor_1_out, nor_2_out);
  nor nor_5 (nor_5_out, nor_2_out, nor_3_out);
  nor nor_6 (Q, nor_4_out, Qbar);
  nor nor_7 (Qbar, Q, nor_5_out);

  // Notes on the sheet:
  //   Clocked SR latch using NOR gates
  //   Clock/enable is level-sensitive.
endmodule

module _29_SR_latch_using_NAND_gates (
  input  Sbar,
  input  Rbar,
  output Q,
  output Qbar
);

  nand nand_1 (Q, Sbar, Qbar);
  nand nand_2 (Qbar, Q, Rbar);

  // Notes on the sheet:
  //   SR latch using NAND gates
  //   Cross-coupled latch; NAND inputs are active-low.
endmodule

module _30_SR_latch_using_NOR_gates (
  input  R,
  input  S,
  output Q,
  output Qbar
);

  nor nor_1 (Q, R, Qbar);
  nor nor_2 (Qbar, Q, S);

  // Notes on the sheet:
  //   SR latch using NOR gates
  //   Cross-coupled latch; NOR inputs are active-high.
endmodule

module _31_3_bit_seven_segment_display (
  input  A,
  input  B,
  input  C,
  output a_2,
  output b_2,
  output c_2,
  output d,
  output e,
  output f,
  output g
);

  wire and_1_out, and_2_out, and_3_out, and_4_out, and_5_out, and_6_out, and_7_out, and_8_out, and_9_out,
       not_1_out, not_2_out, not_3_out, or_4_out;

  not not_1 (not_1_out, A);
  not not_2 (not_2_out, B);
  not not_3 (not_3_out, C);
  and and_1 (and_1_out, A, C);
  and and_2 (and_2_out, not_1_out, not_3_out);
  and and_3 (and_3_out, not_2_out, not_3_out);
  and and_4 (and_4_out, B, C);
  and and_5 (and_5_out, not_1_out, B);
  and and_6 (and_6_out, B, not_3_out);
  and and_7 (and_7_out, A, not_2_out, C);
  and and_8 (and_8_out, A, not_2_out);
  and and_9 (and_9_out, A, not_3_out);
  or or_1 (a_2, B, and_1_out, and_2_out);
  or or_2 (b_2, not_1_out, and_3_out, and_4_out);
  or or_3 (c_2, A, not_2_out, C);
  or or_4 (or_4_out, and_2_out, and_5_out, and_6_out);
  or or_5 (e, and_2_out, and_6_out);
  or or_6 (f, and_3_out, and_8_out, and_9_out);
  or or_7 (g, and_5_out, and_8_out, and_9_out);
  or or_8 (d, or_4_out, and_7_out);

  // Notes on the sheet:
  //   3-bit seven-segment display
  //   Common-cathode outputs (active-high); A is MSB and C is LSB for digits 0-7.
endmodule

module _32_XNOR_gate_using_NAND_gates (
  input  A,
  input  B,
  output Y
);

  wire nand_1_out, nand_2_out, nand_3_out, nand_4_out;

  nand nand_1 (nand_1_out, A, B);
  nand nand_2 (nand_2_out, A, nand_1_out);
  nand nand_3 (nand_3_out, B, nand_1_out);
  nand nand_4 (nand_4_out, nand_2_out, nand_3_out);
  nand nand_5 (Y, nand_4_out, nand_4_out);

  // Notes on the sheet:
  //   XNOR gate using NAND gates
  //   NAND implementation of Y=(A XOR B)'.
endmodule

module _33_XNOR_gate_using_NOR_gates (
  input  A,
  input  B,
  output Y
);

  wire nor_1_out, nor_2_out, nor_3_out;

  nor nor_1 (nor_1_out, A, B);
  nor nor_2 (nor_2_out, A, nor_1_out);
  nor nor_3 (nor_3_out, B, nor_1_out);
  nor nor_4 (Y, nor_2_out, nor_3_out);

  // Notes on the sheet:
  //   XNOR gate using NOR gates
  //   Four-NOR XNOR network.
endmodule

module _34_XOR_gate_using_NAND_gates (
  input  A,
  input  B,
  output Y
);

  wire nand_1_out, nand_2_out, nand_3_out;

  nand nand_1 (nand_1_out, A, B);
  nand nand_2 (nand_2_out, A, nand_1_out);
  nand nand_3 (nand_3_out, B, nand_1_out);
  nand nand_4 (Y, nand_2_out, nand_3_out);

  // Notes on the sheet:
  //   XOR gate using NAND gates
  //   Four-NAND XOR network.
endmodule

module _35_XOR_gate_using_NOR_gates (
  input  A,
  input  B,
  output Y
);

  wire nor_1_out, nor_2_out, nor_3_out, nor_4_out;

  nor nor_1 (nor_1_out, A, B);
  nor nor_2 (nor_2_out, A, nor_1_out);
  nor nor_3 (nor_3_out, B, nor_1_out);
  nor nor_4 (nor_4_out, nor_2_out, nor_3_out);
  nor nor_5 (Y, nor_4_out, nor_4_out);

  // Notes on the sheet:
  //   XOR gate using NOR gates
  //   NOR-only XOR network.
endmodule

module _36_AND_gate (
  input  A,
  input  B,
  output Y
);

  and and_1 (Y, A, B);

  // Notes on the sheet:
  //   AND gate
  //   Y = A . B
endmodule

module _37_OR_gate (
  input  A,
  input  B,
  output Y
);

  or or_1 (Y, A, B);

  // Notes on the sheet:
  //   OR gate
  //   Y = A + B
endmodule

module _38_NOT_gate (
  input  A,
  output Y
);

  not not_1 (Y, A);

  // Notes on the sheet:
  //   NOT gate
  //   Y = A'
endmodule

module _39_XOR_gate (
  input  A,
  input  B,
  output Y
);

  xor xor_1 (Y, A, B);

  // Notes on the sheet:
  //   XOR gate
  //   Y = A XOR B
endmodule

module _40_XNOR_gate (
  input  A,
  input  B,
  output Y
);

  xnor xnor_1 (Y, A, B);

  // Notes on the sheet:
  //   XNOR gate
  //   Y = (A XOR B)'
endmodule

module _41_NOR_gate (
  input  A,
  input  B,
  output Y
);

  nor nor_1 (Y, A, B);

  // Notes on the sheet:
  //   NOR gate
  //   Y = (A + B)'
endmodule

module _42_NAND_gate (
  input  A,
  input  B,
  output Y
);

  nand nand_1 (Y, A, B);

  // Notes on the sheet:
  //   NAND gate
  //   Y = (A . B)'
endmodule

module _43_T_flip_flop_using_NAND_gates (
  input  T,
  input  CLK,
  input  CLR_bar,
  output Q,
  output Qbar
);

  wire nand_1_out, nand_2_out, nand_3_out, nand_4_out, nand_5_out, nand_6_out, nand_7_out;

  nand nand_1 (nand_1_out, Qbar, T, CLK);
  nand nand_2 (nand_2_out, CLK, T, Q);
  nand nand_3 (nand_3_out, nand_1_out, nand_4_out);
  nand nand_4 (nand_4_out, nand_3_out, CLR_bar, nand_2_out);
  nand nand_5 (nand_5_out, CLK, CLK);
  nand nand_6 (nand_6_out, nand_3_out, nand_5_out);
  nand nand_7 (nand_7_out, nand_5_out, nand_4_out);
  nand nand_8 (Q, nand_6_out, Qbar);
  nand nand_9 (Qbar, nand_7_out, CLR_bar, Q);

  // Notes on the sheet:
  //   T flip-flop using NAND gates
  //   T=1 toggles; T=0 holds. Falling-edge master-slave implementation with CLR_bar.
endmodule

module _44_F_A_B_C_A_B_BC_AC (
  input  A,
  input  B,
  input  C,
  output F
);

  wire nor_1_out, nor_2_out, nor_3_out, nor_4_out, nor_5_out, nor_6_out, nor_7_out;

  nor nor_1 (nor_1_out, A, A);
  nor nor_2 (nor_2_out, B, B);
  nor nor_3 (nor_3_out, C, C);
  nor nor_4 (nor_4_out, A, nor_2_out);
  nor nor_5 (nor_5_out, nor_2_out, C);
  nor nor_6 (nor_6_out, nor_1_out, nor_3_out);
  nor nor_7 (nor_7_out, nor_4_out, nor_5_out, nor_6_out);
  nor nor_8 (F, nor_7_out, nor_7_out);

  // Notes on the sheet:
  //   F(A,B,C) = A'B + BC' + AC
  //   NOR-only realization of F(A,B,C) = A'B + BC' + AC.
endmodule

module _45_F_A_B_C_D_A_B_CD_AB_D (
  input  A,
  input  B,
  input  C,
  input  D,
  output F
);

  wire and_1_out, and_2_out, and_3_out, not_1_out, not_2_out, not_3_out;

  not not_1 (not_1_out, A);
  not not_2 (not_2_out, B);
  not not_3 (not_3_out, D);
  and and_1 (and_1_out, not_1_out, B);
  and and_2 (and_2_out, C, not_3_out);
  and and_3 (and_3_out, A, not_2_out, D);
  or or_1 (F, and_1_out, and_2_out, and_3_out);

  // Notes on the sheet:
  //   F(A,B,C,D) = A'B + CD' + AB'D
  //   Representative expression used because the index page does not specify F.
endmodule

module _46_F_A_B_C_D_A_B_CD_AB_D (
  input  A,
  input  B,
  input  C,
  input  D,
  output F
);

  wire nand_1_out, nand_2_out, nand_3_out, nand_4_out, nand_5_out, nand_6_out;

  nand nand_1 (nand_1_out, A, A);
  nand nand_2 (nand_2_out, B, B);
  nand nand_3 (nand_3_out, D, D);
  nand nand_4 (nand_4_out, nand_1_out, B);
  nand nand_5 (nand_5_out, C, nand_3_out);
  nand nand_6 (nand_6_out, A, nand_2_out, D);
  nand nand_7 (F, nand_4_out, nand_5_out, nand_6_out);

  // Notes on the sheet:
  //   F(A,B,C,D) = A'B + CD' + AB'D
  //   NAND-only realization of F(A,B,C,D) = A'B + CD' + AB'D.
endmodule

module _47_NOT_gate_using_NAND_gate (
  input  A,
  output Y
);

  nand nand_1 (Y, A, A);

  // Notes on the sheet:
  //   NOT gate using NAND gate
  //   Tie both NAND inputs to A.
endmodule

module _48_NOT_gate_using_NOR_gate (
  input  A,
  output Y
);

  nor nor_1 (Y, A, A);

  // Notes on the sheet:
  //   NOT gate using NOR gate
  //   Tie both NOR inputs to A.
endmodule

module _49_F_A_B_A_B_AB (
  input  A,
  input  B,
  output F
);

  wire and_1_out, and_2_out, not_1_out, not_2_out;

  not not_1 (not_1_out, A);
  not not_2 (not_2_out, B);
  and and_1 (and_1_out, not_1_out, B);
  and and_2 (and_2_out, A, not_2_out);
  or or_1 (F, and_1_out, and_2_out);

  // Notes on the sheet:
  //   F(A,B) = A'B + AB'
  //   Representative two-variable expression; equals A XOR B.
endmodule

module _50_F_A_B_A_B_AB (
  input  A,
  input  B,
  output F
);

  wire nand_1_out, nand_2_out, nand_3_out, nand_4_out;

  nand nand_1 (nand_1_out, A, A);
  nand nand_2 (nand_2_out, B, B);
  nand nand_3 (nand_3_out, nand_1_out, B);
  nand nand_4 (nand_4_out, A, nand_2_out);
  nand nand_5 (F, nand_3_out, nand_4_out);

  // Notes on the sheet:
  //   F(A,B) = A'B + AB'
  //   NAND-only realization of the representative two-variable expression.
endmodule
